# Fritzing sketch IREmitterDetector (saved by Fritzing 0.7.11b)
breadboards: 1

parts:
  Q1 = NPN-Transistor [package="TO92 [THT]"]
  R1 = Resistor [tolerance=±5% resistance=220 package=THT]  # not connected
  R2 = Resistor [tolerance=±5% resistance=47 package=THT]
  IR_Emitter = LED - 5mm [color="Infrared (850nm)" package="5 mm [THT]"]
  R3 = Resistor [tolerance=±5% resistance=100 package=THT]
  R4 = Resistor [tolerance=±5% resistance=1k package=THT]
  Emitter_Indicator = LED - 5mm [color="Green (555nm)" package="5 mm [THT]"]
  Q2 = PNP-Transistor [package="TO92 [THT]"]
  R5 = Resistor [tolerance=±5% resistance=1k package=THT]
  Threshold_Indicator = LED - 5mm [color="Red (633nm)" package="5 mm [THT]"]
  R6 = Resistor [tolerance=±5% resistance=100k package=THT]
  IR_Detector = LED - 5mm [color="Infrared (850nm)" package="5 mm [THT]"]
  Threshold_Trim = Trimmer Potentiometer [maximum_resistance=10kΩ package=THT]
  Arduino1 = Arduino

nets:
  N1: Q1.E, Emitter_Indicator.cathode, Threshold_Indicator.cathode, IR_Detector.anode, Threshold_Trim.leg1, Arduino1.GND
  N2: Q1.B, R3.Pin_1
  N3: Q1.C, IR_Emitter.cathode
  N4: R2.Pin_0, Q2.C, Threshold_Trim.leg2, Arduino1.+5V
  N5: R2.Pin_1, IR_Emitter.anode
  N6: R3.Pin_0, R4.Pin_0, Arduino1.D9
  N7: R4.Pin_1, Emitter_Indicator.anode
  N8: Q2.E, R5.Pin_0
  N9: Q2.B, R6.Pin_1
  N10: R5.Pin_1, Threshold_Indicator.anode
  N11: R6.Pin_0, IR_Detector.cathode, Arduino1.A0
  N12: Threshold_Trim.wiper, Arduino1.A1
