# Fritzing sketch SevenSegmentDisplay (saved by Fritzing 0.7.11b)
breadboards: 1

parts:
  7_Segment1 = 7 Segment Display
  Arduino1 = Arduino
  R2 = Trimmer Potentiometer [maximum_resistance=10kΩ package=THT]
  R3 = Resistor [tolerance=±5% resistance=1k package=THT]

nets:
  N1: 7_Segment1.Segment_G, Arduino1.D8
  N2: 7_Segment1.Segment_F, Arduino1.D7
  N3: 7_Segment1.common_anode, R3.Pin_1
  N4: 7_Segment1.Segment_E, Arduino1.D6
  N5: 7_Segment1.Segment_D, Arduino1.D5
  N6: 7_Segment1.Segment_DP, Arduino1.D9
  N7: 7_Segment1.Segment_C, Arduino1.D4
  N8: 7_Segment1.Segment_B, Arduino1.D3
  N9: 7_Segment1.Segment_A, Arduino1.D2
  N10: Arduino1.GND, R2.leg1
  N11: Arduino1.+5V, R3.Pin_0
  N12: Arduino1.A0, R2.wiper
